# Fritzing sketch BsidesBoise2017 (saved by Fritzing 0.9.3b)
circuit board: 8.46667cm x 5.64444cm
breadboards: 1

parts:
  LED1 = RGB LED (com. cathode, rgb) [package="5 mm [THT]"]
  LED2 = RGB LED (com. cathode, rgb) [package="5 mm [THT]"]
  LED3 = RGB LED (com. cathode, rgb) [package="5 mm [THT]"]
  LED4 = RGB LED (com. cathode, rgb) [package="5 mm [THT]"]
  D1 = Zener Diode [part_number=1N4732A breakdown_voltage=3.6V package="Melf DO-213 AB [SMD]"]
  VCC1 = Battery
  U1 = NodeMCU V3.0

nets:
  N1: LED1.red_anode, U1.S3
  N2: LED1.common_cathode, LED2.green_anode, LED3.green_anode, LED4.common_cathode, VCC1.-, U1.GND#6, U1.GND#13, U1.GND#16, U1.GND#33
  N3: LED1.green_anode, U1.D0
  N4: LED1.blue_anode, U1.D1
  N5: LED2.red_anode, U1.D4
  N6: LED2.common_cathode, U1.D3
  N7: LED2.blue_anode, U1.D2
  N8: LED3.red_anode, U1.TX
  N9: LED3.common_cathode, U1.RX
  N10: LED3.blue_anode, U1.D8
  N11: LED4.red_anode, U1.D7
  N12: LED4.green_anode, U1.D6
  N13: LED4.blue_anode, U1.D5
  N14: D1.cathode, U1.Vin
  N15: D1.anode, VCC1.+

custom parts:
  NodeMCU V3.0: ESP8266 based NodeMCU
